// Logisim project ANDGate.circ as structural Verilog: 1 circuit, main circuit main
module main (
  input  x,
  input  z,
  input  y
);

  wire not_1_out, or_1_out;

  or or_1 (or_1_out, x, y);
  not not_1 (not_1_out, or_1_out);
endmodule
