// Logisim project Lab0part1.circ as structural Verilog: 1 circuit, main circuit main
module main (
  input  in_1,
  input  in_2
);

  wire and_1_out, and_2_out, not_1_out, not_2_out;

  not not_1 (not_1_out, in_1);
  not not_2 (not_2_out, in_2);
  and and_1 (and_1_out, not_1_out, in_2);
  and and_2 (and_2_out, in_1, not_2_out);
  // OR_Gate or_1 has open pins: in0=and_1_out, in1=and_2_out, out=open

  // Notes on the sheet:
  //   XOR Circuit built using Logism
endmodule
