// Logisim project Lab0part2.circ as structural Verilog: 1 circuit, main circuit main
module main (
  input  [3:0] in_1,
  input  [3:0] in_2
);

  wire [3:0] and_1_out, and_2_out, not_1_out, not_2_out;

  assign not_1_out = ~in_1;  // NOT_Gate not_1, 4 bits wide
  assign not_2_out = ~in_2;  // NOT_Gate not_2, 4 bits wide
  assign and_1_out = not_1_out & in_2;  // AND_Gate and_1, 4 bits wide
  assign and_2_out = in_1 & not_2_out;  // AND_Gate and_2, 4 bits wide
  // OR_Gate or_1 has open pins: in0=and_1_out, in1=and_2_out, out=open

  // Notes on the sheet:
  //   XOR Circuit built using Logism
endmodule
