// Logisim project Lab1Part4.circ as structural Verilog: 1 circuit, main circuit main
module main (
  input  weekend,
  input  sunny,
  output tennis,
  output Rocketball,
  output hiking,
  output stayAtHome
);

  wire not_1_out, not_2_out;

  not not_1 (not_1_out, weekend);
  and and_1 (hiking, weekend, sunny);
  not not_2 (not_2_out, sunny);
  nor nor_1 (stayAtHome, weekend, sunny);
  and and_2 (tennis, sunny, not_1_out);
  and and_3 (Rocketball, not_2_out, weekend);
endmodule
