// Logisim project Lab3.circ as structural Verilog: 4 circuits, main circuit Part1a
module Part1a (
  input  w,
  input  x,
  input  y,
  input  z,
  output F
);

  wire and_1_out, and_2_out, and_3_out, and_4_out, and_5_out, and_6_out, and_7_out, and_8_out, not_1_out,
       not_2_out, not_3_out, not_4_out, or_1_out, or_2_out;

  not not_1 (not_1_out, w);
  not not_2 (not_2_out, x);
  not not_3 (not_3_out, y);
  not not_4 (not_4_out, z);
  and and_1 (and_1_out, not_1_out, not_3_out, not_4_out);
  and and_2 (and_2_out, not_1_out, not_2_out, not_3_out);
  and and_3 (and_3_out, not_2_out, not_3_out, not_4_out);
  and and_4 (and_4_out, w, x, z);
  and and_5 (and_5_out, w, x, y);
  and and_6 (and_6_out, x, y, z);
  and and_7 (and_7_out, not_2_out, not_1_out, not_4_out);
  and and_8 (and_8_out, w, y, z);
  or or_1 (or_1_out, and_1_out, and_2_out, and_3_out, and_4_out);
  or or_2 (or_2_out, and_5_out, and_6_out, and_8_out, and_7_out);
  or or_3 (F, or_1_out, or_2_out);

  // Notes on the sheet:
  //   w'y'z' + w'x'y' + x'y'z'+wxz + wxy + xyz + wyz + w'x'z' 
endmodule

module Part1b (
  input  z,
  input  w,
  input  y,
  input  x,
  output F
);

  wire nand_1_out, nand_2_out, nand_3_out, nand_4_out, nand_5_out, nand_6_out, nand_7_out, nand_8_out,
       nand_9_out, nand_10_out, nand_11_out, nand_12_out, nand_13_out, nand_14_out, nand_15_out, nand_16_out;

  nand nand_1 (nand_1_out, w, w);
  nand nand_2 (nand_2_out, x, x);
  nand nand_3 (nand_3_out, y, y);
  nand nand_4 (nand_4_out, z, z);
  nand nand_5 (nand_5_out, nand_1_out, nand_3_out, nand_4_out);
  nand nand_6 (nand_6_out, nand_1_out, nand_2_out, nand_3_out);
  nand nand_7 (nand_7_out, nand_2_out, nand_3_out, nand_4_out);
  nand nand_8 (nand_8_out, w, x, z);
  nand nand_9 (nand_9_out, w, x, y);
  nand nand_10 (nand_10_out, x, y, z);
  nand nand_11 (nand_11_out, w, y, z);
  nand nand_12 (nand_12_out, nand_2_out, nand_1_out, nand_4_out);
  nand nand_13 (nand_13_out, nand_5_out, nand_6_out, nand_7_out, nand_8_out);
  nand nand_14 (nand_14_out, nand_13_out, nand_13_out);
  nand nand_15 (nand_15_out, nand_16_out, nand_16_out);
  nand nand_16 (nand_16_out, nand_9_out, nand_10_out, nand_11_out, nand_12_out);
  nand nand_17 (F, nand_14_out, nand_15_out);

  // Notes on the sheet:
  //   w'y'z' + w'x'y' + x'y'z'+wxz + wxy + xyz + wyz + w'x'z' 
endmodule

module Part2 (
  input  w,
  input  x,
  input  y,
  input  z,
  output P
);

  wire xor_1_out, xor_2_out;

  xor xor_1 (xor_1_out, w, x);
  xor xor_2 (xor_2_out, y, z);
  xor xor_3 (P, xor_1_out, xor_2_out);
endmodule

module Part3WithExtraCredit (
  input  B0,
  input  B1,
  input  B2,
  input  B3
);

  wire Aa_out, and_1_out, and_2_out, and_3_out, and_4_out, and_5_out, and_6_out, and_7_out, and_8_out,
       and_9_out, and_10_out, and_11_out, and_12_out, and_13_out, and_14_out, and_15_out, and_16_out,
       and_17_out, and_18_out, and_19_out, and_20_out, and_21_out, and_22_out, and_23_out, and_24_out,
       and_25_out, and_26_out, and_27_out, and_28_out, and_29_out, and_30_out, B_out, C_out, D_out, E_out,
       F_out, G_out, not_1_out, not_2_out, not_3_out, not_4_out;

  not not_1 (not_1_out, B0);
  not not_2 (not_2_out, B1);
  not not_3 (not_3_out, B2);
  and and_1 (and_1_out, B3, not_3_out);
  not not_4 (not_4_out, B3);
  and and_2 (and_2_out, not_3_out, not_4_out);
  and and_3 (and_3_out, B2, B3);
  and and_4 (and_4_out, not_1_out, not_2_out, not_3_out);
  and and_5 (and_5_out, B0, B1);
  and and_6 (and_6_out, B0, not_2_out);
  and and_7 (and_7_out, B0, B1);
  and and_8 (and_8_out, not_1_out, B3);
  and and_9 (and_9_out, B0, B2);
  and and_10 (and_10_out, not_3_out, not_1_out);
  and and_11 (and_11_out, B3, not_2_out, not_1_out);
  or G (G_out, and_2_out, and_3_out, and_4_out, and_5_out, and_6_out);
  and and_12 (and_12_out, B2, B0);
  and and_13 (and_13_out, B1, B0);
  or F (F_out, and_1_out, and_10_out, and_11_out, and_12_out, and_13_out);
  _7_Segment_Display A (.g(G_out), .f(F_out), .a(Aa_out), .b(B_out), .e(E_out), .d(D_out), .c(C_out));  // open: dp
  or E (E_out, and_8_out, and_9_out);
  and and_14 (and_14_out, B0, not_2_out, B2);
  and and_15 (and_15_out, B0, B1);
  and and_16 (and_16_out, B3, B1);
  or D (D_out, and_14_out, and_15_out, and_17_out, and_18_out);
  and and_17 (and_17_out, not_1_out, B3);
  and and_18 (and_18_out, not_3_out, not_4_out);
  and and_19 (and_19_out, not_2_out, not_1_out);
  and and_20 (and_20_out, B2, B0);
  or B (B_out, and_24_out, and_25_out, and_26_out);
  or C (C_out, and_27_out, and_28_out, and_29_out, and_30_out);
  and and_21 (and_21_out, not_4_out, not_3_out);
  and and_22 (and_22_out, B3, B2);
  or Aa (Aa_out, and_16_out, and_19_out, and_20_out, and_21_out, and_22_out, and_23_out);
  and and_23 (and_23_out, B2, not_2_out, B0);
  and and_24 (and_24_out, B2, not_1_out);
  and and_25 (and_25_out, not_3_out, not_2_out, B0);
  and and_26 (and_26_out, B1, not_1_out);
  and and_27 (and_27_out, not_3_out, not_1_out);
  and and_28 (and_28_out, not_3_out, not_2_out, B0);
  and and_29 (and_29_out, not_4_out, B2, not_1_out);
  and and_30 (and_30_out, not_2_out, not_1_out);
endmodule
