// Logisim project Lab4.circ as structural Verilog: 5 circuits, main circuit main
module Part1full_adder (
  input  x,
  input  y,
  input  Cin,
  output Sum,
  output Carry
);

  wire p1half_adder_1_carry, p1half_adder_1_sum, p1half_adder_2_carry;

  P1half_adder p1half_adder_1 (.x(x), .y(y), .Sum(p1half_adder_1_sum), .Carry(p1half_adder_1_carry));
  P1half_adder p1half_adder_2 (.x(p1half_adder_1_sum), .y(Cin), .Sum(Sum), .Carry(p1half_adder_2_carry));
  or or_1 (Carry, p1half_adder_2_carry, p1half_adder_1_carry);
endmodule

module main (
  input  x,
  input  y,
  input  a,
  input  b,
  input  c,
  input  a2,
  input  a1,
  input  a0,
  input  b2,
  input  b1,
  input  b0,
  input  in_12,
  output Sum,
  output Carry,
  output Fsum,
  output Fcarry,
  output out_17,
  output out_18,
  output s2,
  output s1,
  output s0,
  output out_22
);

  wire and_2_out, and_3_out, part1full_adder_3_carry, part1full_adder_4_carry, xor_2_out;

  xor xor_1 (Sum, x, y);
  and and_1 (Carry, x, y);
  xor xor_2 (xor_2_out, a, b);
  and and_2 (and_2_out, a, b);
  Part1full_adder part1full_adder_1 (.x(a), .y(b), .Cin(c), .Sum(out_17), .Carry(out_18));
  Part1full_adder part1full_adder_2 (.x(a2), .y(b2), .Cin(part1full_adder_3_carry), .Sum(s2), .Carry(out_22));
  xor xor_3 (Fsum, xor_2_out, c);
  and and_3 (and_3_out, xor_2_out, c);
  Part1full_adder part1full_adder_3 (
    .x(a1), .y(b1), .Cin(part1full_adder_4_carry), .Sum(s1), .Carry(part1full_adder_3_carry));
  or or_1 (Fcarry, and_3_out, and_2_out);
  Part1full_adder part1full_adder_4 (.x(a0), .y(b0), .Cin(in_12), .Sum(s0), .Carry(part1full_adder_4_carry));

  // Notes on the sheet:
  //   x
  //   y
  //   0
  //   0
  //   0
  //   1
  //   1
  //   0
  //   1
  //   1
  //   half adder
  //   sum
  //   0
  //   1
  //   1
  //   0
  //   carry
  //   0
  //   0
  //   0
  //   1
  //   x
  //   0
  //   0
  //   0
  //   0
  //   1
  //   1
  //   1
  //   1
  //   z
  //   y
  //   0
  //   0
  //   0
  //   0
  //   1
  //   1
  //   0
  //   0
  //   0
  //   1
  //   0
  //   1
  //   1
  //   1
  //   1
  //   1
  //   full adder
  //   sum
  //   0
  //   1
  //   1
  //   0
  //   1
  //   0
  //   0
  //   1
  //   carry
  //   0
  //   0
  //   0
  //   1
  //   0
  //   1
  //   1
  //   1
endmodule

module P1half_adder (
  input  x,
  input  y,
  output Sum,
  output Carry
);

  xor xor_1 (Sum, x, y);
  and and_1 (Carry, x, y);
endmodule

module P1threebit_adder (
  input  a2,
  input  a1,
  input  a0,
  input  b2,
  input  b1,
  input  b0,
  input  in_7,
  output s2,
  output s1,
  output s0,
  output out_11
);

  wire part1full_adder_2_carry, part1full_adder_3_carry;

  Part1full_adder part1full_adder_1 (.x(a2), .y(b2), .Cin(part1full_adder_2_carry), .Sum(s2), .Carry(out_11));
  Part1full_adder part1full_adder_2 (
    .x(a1), .y(b1), .Cin(part1full_adder_3_carry), .Sum(s1), .Carry(part1full_adder_2_carry));
  Part1full_adder part1full_adder_3 (.x(a0), .y(b0), .Cin(in_7), .Sum(s0), .Carry(part1full_adder_3_carry));
endmodule

module part2 (
  input  [1:0] wx,
  input  y,
  input  z,
  output F
);

  wire and_1_out, not_1_out, not_2_out, xor_1_out;

  xor xor_1 (xor_1_out, y, z);
  not not_1 (not_1_out, xor_1_out);
  not not_2 (not_2_out, z);
  and and_1 (and_1_out, y, not_2_out);
  Multiplexer #(.select(2)) multiplexer_1 (
    .in0(not_1_out), .in1(z), .in2(not_1_out), .in3(and_1_out), .out(F), .sel(wx));
endmodule
