// Logisim project NORGates.circ as structural Verilog: 1 circuit, main circuit main
module main (
  input  in_1,
  input  in_2,
  output InvertedOr,
  output TrueOr,
  output NOT_OR
);

  or or_1 (TrueOr, in_1, in_2);
  nor nor_1 (NOT_OR, in_1, in_2);
  not not_1 (InvertedOr, TrueOr);
endmodule
