// Logisim project andNandGates.circ as structural Verilog: 1 circuit, main circuit main
module main (
  input  x,
  input  y,
  output xy,
  output out_4
);

  wire and1_out;

  and and1 (and1_out, x, y);
  not not_1 (xy, and1_out);
  nand nand1 (out_4, x, y);
endmodule
