// Logisim project hw2first.circ as structural Verilog: 1 circuit, main circuit main
module main (
  input  w,
  input  x,
  input  y,
  input  z,
  input  xVal,
  input  yVal,
  output xz,
  output result
);

  wire and_2_out, and_3_out, and_4_out, not_1_out, not_2_out, not_3_out, not_4_out;

  not not_1 (not_1_out, w);
  and and_1 (result, xVal, yVal);
  not not_2 (not_2_out, x);
  not not_3 (not_3_out, y);
  not not_4 (not_4_out, z);
  and and_2 (and_2_out, w, x, not_3_out, not_3_out);
  and and_3 (and_3_out, not_1_out, x, z);
  and and_4 (and_4_out, w, x, y, z);
  or or_1 (xz, and_2_out, and_3_out, and_4_out);

  // Notes on the sheet:
  //   Simplified Version
  //    wxy'z + w'xz + wxyz
endmodule
