// Logisim project hw2q9.circ as structural Verilog: 1 circuit, main circuit main
module main (
  input  a,
  input  b,
  input  c,
  input  bVal,
  output result,
  output out_6
);

  wire and_1_out, and_2_out, and_3_out, and_4_out, not_1_out, not_2_out, not_3_out;

  not not_1 (not_1_out, a);
  not not_2 (not_2_out, b);
  not not_3 (not_3_out, c);
  and and_1 (and_1_out, not_1_out, b, c);
  and and_2 (and_2_out, a, b, not_3_out);
  and and_3 (and_3_out, a, b, c);
  and and_4 (and_4_out, not_1_out, b, not_3_out);
  or or_1 (result, and_1_out, and_2_out, and_3_out, and_4_out);

  assign out_6 = bVal;

  // Notes on the sheet:
  //   Simplified Version
  //   a'bc + abc' + abc + a'bc'
endmodule
