// Logisim project question13_hw3.circ as structural Verilog: 1 circuit, main circuit main
module main (
  input  A,
  input  B,
  input  C,
  input  D,
  output F
);

  wire not_1_out, xor_1_out, xor_2_out;

  xor xor_1 (xor_1_out, A, B);
  xor xor_2 (xor_2_out, C, D);
  not not_1 (not_1_out, xor_1_out);
  and and_1 (F, not_1_out, xor_2_out);
endmodule
