// Logisim project quiz2Circuit.circ as structural Verilog: 1 circuit, main circuit main
module main (
  input  a,
  input  b,
  input  c,
  output F
);

  wire and_1_out, not_1_out, not_2_out, not_3_out, or_1_out, or_2_out;

  not not_1 (not_1_out, a);
  not not_2 (not_2_out, b);
  not not_3 (not_3_out, c);
  or or_1 (or_1_out, c, not_2_out);
  or or_2 (or_2_out, b, not_3_out);
  and and_1 (and_1_out, a, or_1_out, or_2_out);
  or or_3 (F, not_1_out, and_1_out);

  // Notes on the sheet:
  //   F(a, b, c) = a' + a(c + b')(b + c')
endmodule
